# Fritzing sketch Tea Timer (saved by Fritzing 0.9.3b)
breadboards: 1

parts:
  A1 = Waveshare rp2040-zero tht [package=THT]
  OLED1 = OLED Mono 0.56 inch blue or white
  RE1 = Rotary Encoder [package=THT]
  S1 = Momentary Switch [package=ksa_sealed_tac_switch]
  U1 = LIPO-110mAh [package=lipo-110]
  Part1 = Micro Lipo Charger
  J1 = Piezo Speaker

nets:
  VCC: A1.Pin_1, OLED1.VCC, Part1.5V, J1.pin1
  GND: A1.Pin_2, OLED1.GND, RE1.EncoderPinA, S1.4, U1.-, Part1.GND
  N1: A1.Pin_6, OLED1.SCL
  N2: A1.Pin_7, OLED1.SDA
  N3: A1.Pin_17, S1.2
  N4: A1.Pin_19, J1.pin2
  N5: A1.Pin_20, RE1.EncoderPinB
  N6: A1.Pin_21, RE1.EncoderPinC
  N7: U1.+, Part1.VBAT

custom parts:
  Waveshare rp2040-zero tht: .RP2040-Zero, A Low-Cost, High-Performance Pico-Like MCU Board Based On Raspberry Pi Microcontroller RP2040. This varant is THT without the extra connections.
  OLED Mono 0.56 inch blue or white: OLED, I2C 3.3V - 5V Blue and White text versions
  Micro Lipo Charger: Oh so handy, this little lipo charger is so small and easy to use you can keep it on your desk or mount it easily into any project! Simply plug it via any MicroUSB cable into a USB port and a 3.7V/4.2V lithium polymer or lithium ion rechargeable battery into the JST plug on the other end. There are two LEDs - one red and one green. While charging, the red LED is lit. When the battery is fully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
